# Fritzing sketch IR cam latency tester using arduino (saved by Fritzing 0.9.3b)
breadboards: 1

parts:
  Part1 = Arduino Uno (Rev3)
  LED1 = LED - 5mm [color="Infrared (940nm)" part_number="RadioShack 276-0143" package="5 mm [THT]"]
  R1 = Resistor [tolerance=±5% resistance=560 package=THT]

nets:
  N1: Part1.D8, R1.Pin_1
  N2: Part1.GND, LED1.cathode
  N3: LED1.anode, R1.Pin_0

notes:
  Similarly, precise resistor value is not terribly important - ballpark is good enough. This is just what I had on hand.
  For best results, use an LED calculator with the specs of your LED (forward voltage and current) to know your target range.
  Wavelength of IR LED not crucial - any near-IR LED should work (800nm+)
  Wavelength of IR LED not crucial - any near-IR LED should work (800nm+).
  Similarly, precise resistor value is not terribly important - ballpark is good enough. This is just what I had on hand.
  For best results, use an LED calculator with the specs of your LED (forward voltage and current) to know your target range.
  Arduino should be running provided sketch or equivalent that opens serial at 115200, and on any character receive, lights up the LED for 10ms.
