# Fritzing sketch IR cam latency tester using buspirate (saved by Fritzing 0.9.3b)
breadboards: 1

parts:
  R1 = Resistor [tolerance=±5% resistance=560 package=THT]
  LED1 = LED - 5mm [color="Infrared (940nm)" part_number="RadioShack 276-0143" current=100mA package="5 mm [THT]"]
  BP1 = shrouded pin header, 10 pins [form="♂ (shrouded male)"]

nets:
  N1: R1.Pin_0, LED1.anode
  Bus Pirate AUX pin: R1.Pin_1, BP1.pin8
  Bus Pirate GND pin/GND: LED1.cathode, BP1.pin1

notes:
  Resistor value is not terribly important - ballpark is good enough. This is just what I had on hand.
  For best results, use an LED calculator with the specs of your LED (forward voltage and current) to know your target range.
  Wavelength of IR LED not crucial - any near-IR LED should work (800nm+)
  Bus Pirate v3.6 header
  GND
  AUX
